# Fritzing sketch Smart_Plant (saved by Fritzing 1.0.0rc)
breadboards: 1

parts:
  A1 = Particle - Photon2
  SENS2 = SoilWatch 10
  OLED_I2C1 = OLED 128x64 I2C Monochrome Display
  R1 = Resistor [tolerance=±5% power=0.25W resistance=220 package=THT]
  Q1 = PNP-Transistor [package="TO92 [THT]"]
  Relay1 = Relay - 6 pins [package="DIP (Dual Inline) [THT]"]
  R2 = Resistor [tolerance=±5% power=0.25W resistance=2.2k package=THT]
  WATER_PUMP1 = water pump/motor  # not connected
  Grove1 = Grove Dust Sensor
  Part1 = MQ-131 breakout
  Part2 = BME280 Breakout  # not connected

nets:
  VCC: A1.Pin_2, SENS2.VCC, OLED_I2C1.VDD, Relay1.VCC, Grove1.VCC, Part1.DO
  GND: A1.Pin_4, A1.Pin_30, A1.Pin_35, SENS2.GND, OLED_I2C1.GND, Q1.C, Relay1.GND, R2.Pin_0, Grove1.GND, Part1.AO
  N1: A1.Pin_5, Part1.VCC
  N2: A1.Pin_6, SENS2.OUT
  N3: A1.Pin_10, Q1.B, R2.Pin_1
  N4: A1.Pin_17, OLED_I2C1.SCK
  N5: R1.Pin_0, Q1.E, Relay1.IN
  N6: R1.Pin_1, Relay1.ON

custom parts:
  Particle - Photon2: The Photon 2 is a microcontroller and Wi-Fi networking developed by particle. Features: 802.11a/b/g/n Wi-Fi, 2.4 GHz and 5 GHz Integrated PCB antenna Integrated U.FL connector for external antenna Integrated RF switch BLE 5 using same antenna as Wi-Fi Realtek RTL8721DM MCU ARM Cortex M33 CPU, 200 MHz 2048 KB (2 MB) user application maximum size 3072 KB (3 MB) of RAM available to user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
  SoilWatch 10: SoilWatch 10 - Capacitive soil moisture sensor
  Relay - 6 pins: A DIP stand-in part for whatever IC you want. With 6 pins on a 900mil dual inline package (DIP) footprint.
  water pump/motor: WATER PUMP BY ARDUBLOCKTR
  Grove Dust Sensor: PPD42 Grove Dust Sensor
  MQ-131 breakout: SKU: 101282
